# Fritzing sketch SiGame (saved by Fritzing 0.9.3b)

parts:
  Часть1 = Arduino Nano (Rev3.0)
  LED1 = LED - 5mm [color="Red (633nm)" package="5 mm [THT]"]
  S12 = Pushbutton [package="[THT]"]
  U3 = Mystery Part - 3 pins [chip_label=BTN package=THT]
  R1 = Resistor [tolerance=±5% resistance=470 package=THT]
  U4 = Mystery Part - 3 pins [chip_label=BTN package=THT]
  U5 = Mystery Part - 3 pins [chip_label=BTN package=THT]
  U6 = Mystery Part - 3 pins [chip_label=BTN package=THT]
  U7 = Mystery Part - 3 pins [chip_label=BTN package=THT]
  U8 = Mystery Part - 3 pins [chip_label=BTN package=THT]
  U9 = Mystery Part - 3 pins [chip_label=BTN package=THT]
  U10 = Mystery Part - 3 pins [chip_label=BTN package=THT]
  U11 = Mystery Part - 3 pins [chip_label=BTN package=THT]
  U13 = Mystery Part - 3 pins [chip_label=LEDS package=THT]
  U15 = Mystery Part - 5 pins [chip_label=DISPLAY package=THT]
  LED2 = LED - 5mm [color="Red (633nm)" package="5 mm [THT]"]
  S13 = Pushbutton [package="[THT]"]
  R2 = Resistor [tolerance=±5% resistance=470 package=THT]
  LED3 = LED - 5mm [color="Yellow (595nm)" package="5 mm [THT]"]
  S14 = Pushbutton [package="[THT]"]
  R3 = Resistor [tolerance=±5% resistance=470 package=THT]
  LED4 = LED - 5mm [color="Green (565nm)" package="5 mm [THT]"]
  S15 = Pushbutton [package="[THT]"]
  R4 = Resistor [tolerance=±5% resistance=470 package=THT]
  S16 = Toggle Switch [package=THT]
  U18 = Mystery Part - 4 pins [chip_label=TP4056 package=THT]
  U17 = LIPO-110mAh [package=lipo-110]

nets:
  N1: Часть1.D2, U8.S
  N2: Часть1.D3, U11.S
  N3: Часть1.D4, U9.S
  N4: Часть1.D5, U10.S
  N5: Часть1.D6, U4.S
  N6: Часть1.D7, U5.S
  N7: Часть1.D8, U6.S
  N8: Часть1.D9, U7.S
  N9: Часть1.D10, U13.DIN
  N10: Часть1.D11/MOSI, U15.DIN
  N11: Часть1.D12/MISO, U15.CS
  GND: Часть1.GND, U4.GND, U5.GND, U6.GND, U7.GND, U8.GND, U9.GND, U10.GND, U11.GND, U13.GND, U15.GND, S13.Pin_1, S14.Pin_1, S15.Pin_1, S15.Pin_2, S16.COM
  VCC: Часть1.5V, U4.VCC, U5.VCC, U6.VCC, U7.VCC, U8.VCC, U9.VCC, U10.VCC, U11.VCC, U13.VCC, U15.VCC, R2.Pin_0, R3.Pin_0, R4.Pin_0, U18.OUT+
  N12: Часть1.A2, LED4.cathode, S15.Pin_3
  N13: Часть1.A1, LED3.cathode, S14.Pin_3
  N14: Часть1.A0, LED2.cathode, S13.Pin_3
  N15: Часть1.D13/SCK, U15.CLK
  N16: LED1.cathode, S12.Pin_1, S12.Pin_2, U3.S
  N17: LED1.anode, R1.Pin_0
  N18: S12.Pin_3, S12.Pin_4, U3.GND
  N19: U3.VCC, R1.Pin_1
  N20: LED2.anode, R2.Pin_1
  N21: LED3.anode, R3.Pin_1
  N22: LED4.anode, R4.Pin_1
  N23: S16.L2, U18.OUT-
  N24: U18.B-, U17.-
  N25: U18.B+, U17.+

notes:
  Button_Module
  Wires

custom parts:
  Mystery Part - 3 pins: A dummy, proxy, ersatz, stand-in part for whatever you want. With 3 pins on a 100 mil inline pin header footprint.
  Mystery Part - 3 pins: A dummy, proxy, ersatz, stand-in part for whatever you want. With 3 pins on a 100 mil inline pin header footprint.
  Mystery Part - 5 pins: A dummy, proxy, ersatz, stand-in part for whatever you want. With 5 pins on a 100 mil inline pin header footprint.
  Mystery Part - 4 pins: A dummy, proxy, ersatz, stand-in part for whatever you want. With 4 pins on a 100 mil inline pin header footprint.
