# Fritzing sketch SiGame2 (saved by Fritzing 0.9.3b)

parts:
  LED2 = LED - 5mm [color="Red (633nm)" package="5 mm [THT]"]
  S13 = Pushbutton [package="[THT]"]
  U10 = Mystery Part - 3 pins [chip_label=BTN package=THT]
  R2 = Resistor [tolerance=±5% resistance=470 package=THT]
  S17 = Toggle Switch [package=THT]
  U19 = LIPO-110mAh [package=lipo-110]
  U20 = Mystery Part - 4 pins [chip_label=TP4056 package=THT]
  S18 = Pushbutton [package="[THT]"]
  S19 = Pushbutton [package="[THT]"]
  R3 = Resistor [tolerance=±5% resistance=10k package=THT]
  R4 = Resistor [tolerance=±5% resistance=10k package=THT]
  R9 = Resistor [tolerance=±5% resistance=10k package=THT]
  S20 = Pushbutton [package="[THT]"]
  S21 = Pushbutton [package="[THT]"]
  R11 = Resistor [tolerance=±5% resistance=10k package=THT]
  M1 = STM32F103C8T6 blue mini board
  U26 = Mystery Part - 3 pins [chip_label=BTN package=THT]
  U27 = Mystery Part - 3 pins [chip_label=BTN package=THT]
  U28 = Mystery Part - 3 pins [chip_label=BTN package=THT]
  U29 = Mystery Part - 3 pins [chip_label=BTN package=THT]
  U30 = Mystery Part - 3 pins [chip_label=BTN package=THT]
  U31 = Mystery Part - 3 pins [chip_label=BTN package=THT]
  U32 = Mystery Part - 3 pins [chip_label=BTN package=THT]
  U33 = Mystery Part - 3 pins [chip_label=BTN package=THT]
  U35 = Mystery Part - 5 pins [chip_label=DISPLAY package=THT]
  U36 = Mystery Part - 3 pins [chip_label=LEDS package=THT]
  S26 = Pushbutton [package="[THT]"]
  S27 = Pushbutton [package="[THT]"]
  R16 = Resistor [tolerance=±5% resistance=10k package=THT]
  R18 = Resistor [tolerance=±5% resistance=10k package=THT]
  S28 = Pushbutton [package="[THT]"]
  S29 = Pushbutton [package="[THT]"]
  S30 = Pushbutton [package="[THT]"]
  S31 = Pushbutton [package="[THT]"]
  R19 = Resistor [tolerance=±5% resistance=10k package=THT]
  R20 = Resistor [tolerance=±5% resistance=10k package=THT]
  R21 = Resistor [tolerance=±5% resistance=10k package=THT]
  R22 = Resistor [tolerance=±5% resistance=10k package=THT]
  LED3 = LED - 5mm [color="Red (633nm)" package="5 mm [THT]"]
  S32 = Pushbutton [package="[THT]"]
  R23 = Resistor [tolerance=±5% resistance=470 package=THT]
  LED4 = LED - 5mm [color="Red (633nm)" package="5 mm [THT]"]
  S33 = Pushbutton [package="[THT]"]
  R24 = Resistor [tolerance=±5% resistance=470 package=THT]
  LED5 = LED - 5mm [color="Red (633nm)" package="5 mm [THT]"]
  S34 = Pushbutton [package="[THT]"]
  R25 = Resistor [tolerance=±5% resistance=470 package=THT]
  U38 = Mystery Part - 8 pins [chip_label=JUDGE package=THT]
  U41 = Mystery Part - 8 pins [chip_label=JUDGE package=THT]
  Часть1 = Arduino Nano (Rev3.0)
  R26 = Photocell (LDR) [package=THT]
  R27 = Resistor [tolerance=±5% resistance=10k package=THT]
  S35 = Toggle Switch [package=THT]
  S36 = Toggle Switch [package=THT]

nets:
  N1: LED2.cathode, S13.Pin_3, S13.Pin_4, U10.GND
  N2: LED2.anode, R2.Pin_0
  N3: S13.Pin_2, U10.S
  N4: U10.LED, R2.Pin_1
  GND: S17.COM, M1.G, U26.GND, U27.GND, U28.GND, U29.GND, U30.GND, U31.GND, U32.GND, U33.GND, U35.GND, U36.GND, U38.GND, Часть1.GND, R27.Pin_1
  N5: S17.L2, U20.OUT-
  N6: U19.+, U20.B+
  N7: U19.-, U20.B-
  5V: U20.OUT+, M1.5V, U35.VCC, U36.VCC, Часть1.5V, R26.pin_0
  N8: S18.Pin_1, S18.Pin_2, R3.Pin_1, R9.Pin_0, U41.A_P_1_4
  N9: S18.Pin_3, S19.Pin_3, S19.Pin_4, S20.Pin_3, S20.Pin_4, S21.Pin_3, S26.Pin_3, S27.Pin_3, S27.Pin_4, S28.Pin_3, S29.Pin_3, S30.Pin_3, S31.Pin_3, R23.Pin_1, R24.Pin_1, R25.Pin_1, U41.VCC
  N10: S19.Pin_1, S19.Pin_2, R3.Pin_0, R4.Pin_1
  N11: R4.Pin_0, S20.Pin_1, S20.Pin_2, R11.Pin_1
  N12: R9.Pin_1, R16.Pin_1, R20.Pin_1, S32.Pin_3, S32.Pin_4, S33.Pin_4, S34.Pin_3, S34.Pin_4, U41.GND
  N13: S21.Pin_1, S21.Pin_2, R11.Pin_0
  N14: M1.A9, S35.COM
  N15: M1.A10, S36.COM
  N16: M1.A15, U38.INT_MASTER
  N17: M1.B4, U29.S
  N18: M1.B5, U28.S
  N19: M1.B6, U27.S
  3.3V: M1.3.3V, U38.VCC
  N20: M1.A1, U32.S
  N21: M1.A2, U31.S
  N22: M1.A3, U30.S
  N23: M1.A4, U38.A_P_1_4
  N24: M1.A5, U38.A_P_5_8
  N25: M1.A6, U38.A_J_T_F
  N26: M1.A7, U26.S
  N27: M1.B0, U33.S
  N28: M1.B10, U38.INT_SPECIAL
  N29: M1.B11, U38.INT_RESERVED
  N30: U26.LED, Часть1.D2
  N31: U27.LED, Часть1.D3
  N32: U28.LED, Часть1.D4
  N33: U29.LED, Часть1.D5
  N34: U30.LED, Часть1.D6
  N35: U31.LED, Часть1.D7
  N36: U32.LED, Часть1.D8
  N37: U33.LED, Часть1.D9
  N38: U35.DIN, Часть1.D11/MOSI
  N39: U35.CS, Часть1.D12/MISO
  N40: U35.CLK, Часть1.D13/SCK
  N41: U36.DIN, Часть1.A0
  N42: S26.Pin_1, S26.Pin_2, R18.Pin_0
  N43: S27.Pin_1, S27.Pin_2, R16.Pin_0, R18.Pin_1, U41.A_J_T_F
  N44: S28.Pin_1, S28.Pin_2, R19.Pin_0
  N45: S29.Pin_1, S29.Pin_2, R19.Pin_1, R21.Pin_0
  N46: S30.Pin_1, S30.Pin_2, R21.Pin_1, R22.Pin_0
  N47: S31.Pin_1, S31.Pin_2, R20.Pin_0, R22.Pin_1, U41.A_P_5_8
  N48: LED3.cathode, S32.Pin_1, S32.Pin_2, U41.INT_RESERVED
  N49: LED3.anode, R23.Pin_0
  N50: LED4.cathode, S33.Pin_1, S33.Pin_2, U41.INT_MASTER
  N51: LED4.anode, R24.Pin_0
  N52: LED5.cathode, S34.Pin_1, S34.Pin_2, U41.INT_SPECIAL
  N53: LED5.anode, R25.Pin_0
  N54: Часть1.D1/TX, S35.L2
  N55: Часть1.D0/RX, S36.L2
  N56: Часть1.A1, R26.pin_1, R27.Pin_0

notes:
  Player_Module X8
  Wires
  T_F
  P 1-4
  P 5-8
  Judge_Module
  PC
  programming switches
  leds optional

custom parts:
  Mystery Part - 3 pins: A dummy, proxy, ersatz, stand-in part for whatever you want. With 3 pins on a 100 mil inline pin header footprint.
  Mystery Part - 4 pins: A dummy, proxy, ersatz, stand-in part for whatever you want. With 4 pins on a 100 mil inline pin header footprint.
  Mystery Part - 5 pins: A dummy, proxy, ersatz, stand-in part for whatever you want. With 5 pins on a 100 mil inline pin header footprint.
  Mystery Part - 3 pins: A dummy, proxy, ersatz, stand-in part for whatever you want. With 3 pins on a 100 mil inline pin header footprint.
  Mystery Part - 8 pins: A dummy, proxy, ersatz, stand-in part for whatever you want. With 8 pins on a 100 mil inline pin header footprint.
